// Logisim project 32.circ as structural Verilog
module main (
);

  Core_1 core_1_1 ();
  Core_0 core_0_1 ();  // open: OPCODE, A, B, out_4
  L1_Cache l1_cache_1 ();
  L1_Cache l1_cache_2 ();
  L2_Cache l2_cache_1 ();
  L3_Cache l3_cache_1 ();
  Core_3 core_3_1 ();
  Core_2 core_2_1 ();
  L1_Cache l1_cache_3 ();
  L1_Cache l1_cache_4 ();
  L2_Cache l2_cache_2 ();
  Register_part #(.width(32)) register_1 ();  // open: D, en, Q, clk, clr
endmodule

module Core_0 (
  input  [31:0] OPCODE,
  input  [31:0] A,
  input  [31:0] B,
  output [31:0] out_4
);

  wire control_unit_1_clk, undriven;
  wire [3:0] control_unit_1_alu_opcode;
  wire [31:0] alu_1_addout, alu_1_andout, alu_1_dec, alu_1_divout, alu_1_inc, alu_1_multout, alu_1_not,
       alu_1_orout, alu_1_shftl, alu_1_shftr, alu_1_subout, alu_1_xorout, register_1_q, register_2_q;

  Register_part #(.width(32)) register_1 (.D(A), .en(1'b1), .Q(register_1_q), .clk(control_unit_1_clk), .clr(undriven));
  Control_Unit control_unit_1 (.CLK(control_unit_1_clk), .INSTRUCTIONS(OPCODE), .ALU_OPCODE(control_unit_1_alu_opcode));
  Register_part #(.width(32)) register_2 (.D(B), .en(1'b1), .Q(register_2_q), .clk(control_unit_1_clk), .clr(undriven));
  ALU alu_1 (
    .A(register_1_q), .OPCODE(control_unit_1_alu_opcode), .B(register_2_q), .ADDOUT(alu_1_addout),
    .SUBOUT(alu_1_subout), .MULTOUT(alu_1_multout), .DIVOUT(alu_1_divout), .ANDOUT(alu_1_andout),
    .OROUT(alu_1_orout), .XOROUT(alu_1_xorout), .NOT(alu_1_not), .SHFTL(alu_1_shftl), .SHFTR(alu_1_shftr),
    .INC(alu_1_inc), .DEC(alu_1_dec));  // open: in_5, in_4, out_12, out_13, MULT_CARRY, DIV_CARRY, C
  Multiplexer #(.select(4), .width(32)) multiplexer_1 (
    .in1(alu_1_addout), .in2(alu_1_subout), .in3(alu_1_multout), .in4(alu_1_divout), .in5(alu_1_andout),
    .in6(alu_1_orout), .in7(alu_1_xorout), .in8(alu_1_not), .in9(alu_1_shftl), .in10(alu_1_shftr),
    .in11(alu_1_inc), .in12(alu_1_dec), .out(out_4), .sel(control_unit_1_alu_opcode));  // open: in0, in13, in14, in15, en
endmodule

module ALU (
  input  [31:0] A,
  input  [31:0] B,
  input  [3:0] OPCODE,
  input  [31:0] in_4,
  input  in_5,
  output [31:0] ADDOUT,
  output [31:0] SUBOUT,
  output [31:0] MULTOUT,
  output [31:0] DIVOUT,
  output [31:0] ANDOUT,
  output [31:0] OROUT,
  output [31:0] out_12,
  output [31:0] out_13,
  output [31:0] XOROUT,
  output [31:0] NOT,
  output [31:0] SHFTL,
  output [31:0] SHFTR,
  output [31:0] INC,
  output [31:0] DEC,
  output [31:0] MULT_CARRY,
  output [31:0] DIV_CARRY,
  output C
);

  wire undriven;
  wire [4:0] bit_extender_1_out, bit_extender_2_out;
  wire [31:0] demultiplexer_2_out1, demultiplexer_2_out2, demultiplexer_2_out3, demultiplexer_2_out4,
       demultiplexer_2_out5, demultiplexer_2_out6, demultiplexer_2_out7, demultiplexer_2_out8,
       demultiplexer_2_out9, demultiplexer_2_out10, demultiplexer_2_out11, demultiplexer_2_out12,
       demultiplexer_3_out1, demultiplexer_3_out2, demultiplexer_3_out3, demultiplexer_3_out4,
       demultiplexer_3_out5, demultiplexer_3_out6, demultiplexer_3_out7, demultiplexer_3_out9,
       demultiplexer_3_out10;

  Demultiplexer #(.width(32)) demultiplexer_1 (.out0(out_12), .out1(out_13), .in(in_4), .sel(in_5));  // open: en
  Demultiplexer #(.select(4), .width(32), .disabled(0)) demultiplexer_2 (
    .out1(demultiplexer_2_out1), .out2(demultiplexer_2_out2), .out3(demultiplexer_2_out3),
    .out4(demultiplexer_2_out4), .out5(demultiplexer_2_out5), .out6(demultiplexer_2_out6),
    .out7(demultiplexer_2_out7), .out8(demultiplexer_2_out8), .out9(demultiplexer_2_out9),
    .out10(demultiplexer_2_out10), .out11(demultiplexer_2_out11), .out12(demultiplexer_2_out12), .in(A),
    .sel(OPCODE), .en(undriven));  // open: out0, out13, out14, out15
  Demultiplexer #(.select(4), .width(32), .disabled(0)) demultiplexer_3 (
    .out1(demultiplexer_3_out1), .out2(demultiplexer_3_out2), .out3(demultiplexer_3_out3),
    .out4(demultiplexer_3_out4), .out5(demultiplexer_3_out5), .out6(demultiplexer_3_out6),
    .out7(demultiplexer_3_out7), .out9(demultiplexer_3_out9), .out10(demultiplexer_3_out10), .in(B),
    .sel(OPCODE), .en(undriven));  // open: out0, out8, out11, out12, out13, out14, out15
  Bit_Extender #(.in_width(32), .out_width(5)) bit_extender_1 (.in(demultiplexer_3_out9), .out(bit_extender_1_out));
  Bit_Extender #(.in_width(32), .out_width(5)) bit_extender_2 (.in(demultiplexer_3_out10), .out(bit_extender_2_out));
  Arithmatic_functions arithmatic_functions_1 (
    .ADD_A(demultiplexer_2_out1), .ADD_B(demultiplexer_3_out1), .SUB_A(demultiplexer_2_out2),
    .SUB_B(demultiplexer_3_out2), .MULT_A(demultiplexer_2_out3), .MULT_B(demultiplexer_3_out3),
    .DIV_A(demultiplexer_2_out4), .DIV_B(demultiplexer_3_out4), .ADD_A_2(ADDOUT), .SUB_A_2(SUBOUT),
    .MULT_A_2(MULTOUT), .DIV_A_2(DIVOUT), .F_CARRY(C), .MULT_CARRY(MULT_CARRY), .DIV_REM(DIV_CARRY));
  LOGIC_FUNCS logic_funcs_1 (
    .AND_A(demultiplexer_2_out5), .AND_B(demultiplexer_3_out5), .OR_A(demultiplexer_2_out6),
    .OR_B(demultiplexer_3_out6), .XOR_A(demultiplexer_2_out7), .XOR_B(demultiplexer_3_out7),
    .NOT(demultiplexer_2_out8), .AND(ANDOUT), .OR(OROUT), .XOR(XOROUT), .NOT_2(NOT));
  Shifter #(.width(32)) shifter_1 (.in(demultiplexer_2_out9), .\dist (bit_extender_1_out), .out(SHFTL));
  Shifter #(.width(32), .shift("lr")) shifter_2 (.in(demultiplexer_2_out10), .\dist (bit_extender_2_out), .out(SHFTR));
  INC inc_1 (.in_1(demultiplexer_2_out11), .out_2(INC));
  DEC dec_1 (.in_1(demultiplexer_2_out12), .out_2(DEC));
  ALU_INF alu_inf_1 ();  // open: in_1, in_2, in_3, in_4, in_5, in_6, in_7, in_8, in_9, in_10
endmodule

// CONTROL_UNIT
module Control_Unit (
  input  [31:0] INSTRUCTIONS,
  output [3:0] ALU_OPCODE,
  output CLK
);

  Clock clock_1 (.out(CLK));
  Counter #(.width(32), .max('hffffffff)) SQC (.clk(CLK));  // open: load, D, count, Q, carry, clr
  Decoder #(.select(3)) decoder_1 ();  // open: out0, out1, out2, out3, out4, out5, out6, out7, sel, en
  CTRL_LOGIC ctrl_logic_1 (.in_1(INSTRUCTIONS[4:0]), .ALU_OPCODE(ALU_OPCODE));  // open: in_2, in_3
endmodule

// REG
module Register (
  input  [31:0] in_1,
  input  in_2,
  input  in_3,
  output [31:0] out_4
);

  Register_part #(.width(32)) register_1 (.D(in_1), .en(in_3), .Q(out_4), .clk(in_2));  // open: clr
endmodule

// ARTH_FUNCS
module Arithmatic_functions (
  input  [31:0] ADD_A,
  input  [31:0] ADD_B,
  input  [31:0] SUB_A,
  input  [31:0] SUB_B,
  input  [31:0] MULT_A,
  input  [31:0] MULT_B,
  input  [31:0] DIV_A,
  input  [31:0] DIV_B,
  output [31:0] ADD_A_2,
  output [31:0] SUB_A_2,
  output [31:0] MULT_A_2,
  output [31:0] DIV_A_2,
  output F_CARRY,
  output [31:0] MULT_CARRY,
  output [31:0] DIV_REM
);

  wire adder_1_cout, subtractor_1_bout;

  Adder #(.width(32)) adder_1 (.a(ADD_A), .b(ADD_B), .out(ADD_A_2), .cout(adder_1_cout));  // open: cin
  Subtractor #(.width(32)) subtractor_1 (.a(SUB_A), .b(SUB_B), .out(SUB_A_2), .bout(subtractor_1_bout));  // open: bin
  Multiplier #(.width(32)) multiplier_1 (.a(MULT_A), .b(MULT_B), .out(MULT_A_2), .cout(MULT_CARRY));  // open: cin
  Divider #(.width(32)) divider_1 (.a(DIV_A), .b(DIV_B), .out(DIV_A_2), .rem(DIV_REM));  // open: upper
  or or_1 (F_CARRY, adder_1_cout, subtractor_1_bout);
endmodule

module ALU_INF (
  input  [31:0] in_1,
  input  [31:0] in_2,
  input  [31:0] in_3,
  input  [31:0] in_4,
  input  [31:0] in_5,
  input  [31:0] in_6,
  input  [31:0] in_7,
  input  [31:0] in_8,
  input  [31:0] in_9,
  input  [31:0] in_10
);

  wire or_1_out, or_2_out, or_3_out, or_4_out, or_5_out, or_6_out, or_7_out, or_8_out, or_9_out, or_10_out,
       or_11_out, or_12_out, or_13_out, or_14_out, or_15_out, or_16_out, or_17_out, or_18_out, or_19_out,
       or_20_out, or_21_out, or_22_out, or_23_out, or_24_out, or_25_out, or_26_out, or_27_out, or_28_out,
       or_29_out, or_30_out, or_31_out;
  wire [31:0] nor_1_out, nor_2_out, nor_3_out, nor_4_out, nor_5_out, nor_6_out, nor_7_out, nor_8_out,
       nor_9_out;

  assign nor_1_out = ~(in_1 | in_3);  // NOR_Gate nor_1, 32 bits wide
  assign nor_2_out = ~(nor_1_out | nor_3_out);  // NOR_Gate nor_2, 32 bits wide
  assign nor_3_out = ~(in_2 | in_4);  // NOR_Gate nor_3, 32 bits wide
  assign nor_4_out = ~(in_5 | in_6);  // NOR_Gate nor_4, 32 bits wide
  assign nor_5_out = ~(in_7 | in_9);  // NOR_Gate nor_5, 32 bits wide
  assign nor_6_out = ~(nor_5_out | nor_7_out);  // NOR_Gate nor_6, 32 bits wide
  assign nor_7_out = ~(in_8 | in_10);  // NOR_Gate nor_7, 32 bits wide
  Bit_Extender #(.in_width(32), .out_width(1)) bit_extender_1 ();  // open: in, out
  Bit_Extender #(.in_width(32), .out_width(1)) bit_extender_2 ();  // open: in, out
  assign nor_8_out = ~(nor_2_out | nor_9_out);  // NOR_Gate nor_8, 32 bits wide
  assign nor_9_out = ~(nor_4_out | nor_6_out);  // NOR_Gate nor_9, 32 bits wide
  Bit_Extender #(.in_width(32), .out_width(1)) bit_extender_3 ();  // open: in, out
  or or_1 (or_1_out, nor_8_out[0], nor_8_out[2]);
  or or_2 (or_2_out, nor_8_out[1], nor_8_out[3]);
  or or_3 (or_3_out, nor_8_out[4], nor_8_out[6]);
  or or_4 (or_4_out, nor_8_out[5], nor_8_out[7]);
  or or_5 (or_5_out, nor_8_out[8], nor_8_out[10]);
  or or_6 (or_6_out, nor_8_out[9], nor_8_out[11]);
  or or_7 (or_7_out, nor_8_out[12], nor_8_out[14]);
  or or_8 (or_8_out, nor_8_out[13], nor_8_out[15]);
  or or_9 (or_9_out, nor_8_out[16], nor_8_out[18]);
  or or_10 (or_10_out, nor_8_out[17], nor_8_out[19]);
  or or_11 (or_11_out, nor_8_out[20], nor_8_out[22]);
  or or_12 (or_12_out, nor_8_out[21], nor_8_out[23]);
  or or_13 (or_13_out, nor_8_out[24], nor_8_out[26]);
  or or_14 (or_14_out, nor_8_out[25], nor_8_out[27]);
  or or_15 (or_15_out, nor_8_out[28], nor_8_out[30]);
  or or_16 (or_16_out, nor_8_out[29], nor_8_out[31]);
  or or_17 (or_17_out, or_1_out, or_3_out);
  or or_18 (or_18_out, or_2_out, or_4_out);
  or or_19 (or_19_out, or_5_out, or_7_out);
  or or_20 (or_20_out, or_6_out, or_8_out);
  or or_21 (or_21_out, or_9_out, or_11_out);
  or or_22 (or_22_out, or_10_out, or_12_out);
  or or_23 (or_23_out, or_13_out, or_15_out);
  or or_24 (or_24_out, or_14_out, or_16_out);
  or or_25 (or_25_out, or_17_out, or_19_out);
  or or_26 (or_26_out, or_18_out, or_20_out);
  or or_27 (or_27_out, or_21_out, or_23_out);
  or or_28 (or_28_out, or_22_out, or_24_out);
  or or_29 (or_29_out, or_25_out, or_27_out);
  or or_30 (or_30_out, or_26_out, or_28_out);
  or or_31 (or_31_out, or_29_out, or_30_out);
endmodule

module LOGIC_FUNCS (
  input  [31:0] AND_A,
  input  [31:0] AND_B,
  input  [31:0] OR_A,
  input  [31:0] OR_B,
  input  [31:0] XOR_A,
  input  [31:0] XOR_B,
  input  [31:0] NOT,
  output [31:0] AND,
  output [31:0] OR,
  output [31:0] XOR,
  output [31:0] NOT_2
);

  assign AND = AND_A & AND_B;  // AND_Gate and_1, 32 bits wide
  assign OR = OR_A | OR_B;  // OR_Gate or_1, 32 bits wide
  assign XOR = XOR_A ^ XOR_B;  // XOR_Gate xor_1, 32 bits wide
  assign NOT_2 = ~NOT;  // NOT_Gate not_1, 32 bits wide
endmodule

module INC (
  input  [31:0] in_1,
  output [31:0] out_2
);

  Adder #(.width(32)) adder_1 (.a(32'h1), .b(in_1), .out(out_2));  // open: cin, cout
endmodule

module DEC (
  input  [31:0] in_1,
  output [31:0] out_2
);

  Subtractor #(.width(32)) subtractor_1 (.a(32'h1), .b(in_1), .out(out_2));  // open: bin, bout
endmodule

module CTRL_LOGIC (
  input  [4:0] in_1,
  input  in_2,
  input  in_3,
  output [3:0] ALU_OPCODE
);

  Decoder #(.select(5)) decoder_1 (
    .out28(ALU_OPCODE[3]), .out29(ALU_OPCODE[2]), .out30(ALU_OPCODE[1]), .out31(ALU_OPCODE[0]), .sel(in_1));  // open: out0, out1, out2, out3, out4, out5, out6, out7, out8, out9, out10, out11, out12, out13, out14, out15, out16, out17, out18, out19, out20, out21, out22, out23, out24, out25, out26, out27, en
endmodule
